# Fritzing sketch Schaltung_Hauptsteuerung (saved by Fritzing 0.9.3b)

parts:
  Hauptsteuerung = Arduino Mega 2560 (Rev3)
  Motortreiber_0 = Pololu A4988 [package=SO16]
  Motortreiber_1 = Pololu A4988 [package=SO16]
  Motortreiber_2 = Pololu A4988 [package=SO16]
  Motor_0 = Stepper Motor - Bipolar
  Motor_1 = Stepper Motor - Bipolar
  Motor_2 = Stepper Motor - Bipolar
  Sensoren_Tisch_1 = Infrared Proximity Sensor
  Sensoren_Tisch_2 = Infrared Proximity Sensor
  Sensoren_Tisch_0 = Infrared Proximity Sensor

nets:
  N1: Hauptsteuerung.A8, Hauptsteuerung.A9, Hauptsteuerung.A10, Hauptsteuerung.A11, Hauptsteuerung.A12, Hauptsteuerung.A13, Sensoren_Tisch_2.Vout
  N2: Hauptsteuerung.A0, Hauptsteuerung.A1, Hauptsteuerung.A2, Hauptsteuerung.A3, Hauptsteuerung.A4, Hauptsteuerung.A5, Sensoren_Tisch_1.Vout
  N3: Hauptsteuerung.D6_PWM, Hauptsteuerung.D47
  N4: Hauptsteuerung.D22, Hauptsteuerung.D23, Hauptsteuerung.D24, Hauptsteuerung.D25, Hauptsteuerung.D26, Hauptsteuerung.D27, Sensoren_Tisch_0.Vout
  N5: Hauptsteuerung.D44, Motortreiber_0.ENABLE
  N6: Hauptsteuerung.D45, Motortreiber_1.ENABLE
  N7: Hauptsteuerung.D46, Motortreiber_2.ENABLE
  GND: Motortreiber_0.GND, Motortreiber_1.GND, Motortreiber_2.GND
  N8: Motortreiber_0.1B, Motor_0.D
  N9: Motortreiber_0.1A, Motor_0.B
  N10: Motortreiber_0.2A, Motor_0.C
  N11: Motortreiber_0.2B, Motor_0.A
  12V: Motortreiber_0.VMOT, Motortreiber_1.VMOT, Motortreiber_2.VMOT
  N12: Motortreiber_1.1B, Motor_1.D
  N13: Motortreiber_1.1A, Motor_1.B
  N14: Motortreiber_1.2A, Motor_1.C
  N15: Motortreiber_1.2B, Motor_1.A
  N16: Motortreiber_2.1B, Motor_2.D
  N17: Motortreiber_2.1A, Motor_2.B
  N18: Motortreiber_2.2A, Motor_2.C
  N19: Motortreiber_2.2B, Motor_2.A
